// Logisim project t3.circ as structural Verilog: 7 circuits, main circuit main
module main (
);

  wire and_1_out, branchOK, brzrOK, clk, ji, jr, or_1_out, reset;
  wire [7:0] adder_1_out, B, imm8, multiplexer_1_out;
  wire [31:0] multiplexer_2_out, PC;

  Button u_reset (.out(reset));
  Multiplexer #(.width(8)) multiplexer_1 (.in0(8'h1), .in1(imm8), .out(multiplexer_1_out), .sel(ji));
  and and_1 (and_1_out, brzrOK, branchOK);
  Clock #(.highDuration(2), .lowDuration(2), .phaseOffset(1)) clock_1 (.out(clk));
  Adder adder_1 (.a(multiplexer_1_out), .out(adder_1_out));  // open: b, cin, cout
  or or_1 (or_1_out, jr, and_1_out);
  Adder #(.width(32)) adder_2 (.a(PC), .b(32'h20));  // open: out, cin, cout
  Multiplexer #(.width(8)) multiplexer_2 (.in0(adder_1_out), .in1(B), .out(multiplexer_2_out[7:0]), .sel(or_1_out));
  Register #(.width(32)) u_PC (.D(multiplexer_2_out), .en(1'b1), .clk(clk), .clr(reset));  // open: Q
  Register #(.width(32)) register_1 (.Q(PC));  // open: D, en, clk, clr
  extSinal8bits extsinal8bits_1 ();  // open: imm4, imm8
  movhighmovlow movhighmovlow_1 ();  // open: A, imm, Seletor, R
  BancoReg bancoreg_1 ();  // open: clk, d, w, SelW, SelA, SelB, reset, A, B
  ULA ula_1 ();  // open: A, B, Seletor, brzr, R
  ULA ula_2 ();  // open: A, B, Seletor, brzr, R
  // Pins of 8 and 32 bits meet at multiplexer_2_out

  // Notes on the sheet:
  //   TODO alterar com os sinais de controle
  //   brzr e jr
endmodule

module BancoReg (
  input  clk,
  input  [7:0] d,
  input  w,
  input  [1:0] SelW,
  input  [1:0] SelA,
  input  [1:0] SelB,
  input  reset,
  output [7:0] A,
  output [7:0] B
);

  wire w0, w1, w2, w3;
  wire [7:0] l0, l1, l2, l3;

  Demultiplexer #(.select(2)) demultiplexer_1 (.out0(w0), .out1(w1), .out2(w2), .out3(w3), .in(w), .sel(SelW));
  Multiplexer #(.select(2), .width(8)) multiplexer_1 (.in0(l0), .in1(l1), .in2(l2), .in3(l3), .out(A), .sel(SelA));
  Multiplexer #(.select(2), .width(8)) multiplexer_2 (.in0(l0), .in1(l1), .in2(l2), .in3(l3), .out(B), .sel(SelB));
  Register r0 (.D(d), .en(w0), .clk(clk), .Q(l0), .clr(reset));
  Register r1 (.D(d), .en(w1), .clk(clk), .Q(l1), .clr(reset));
  Register r2 (.D(d), .en(w2), .clk(clk), .Q(l2), .clr(reset));
  Register r3 (.D(d), .en(w3), .clk(clk), .Q(l3), .clr(reset));

  // Other names for the same wires on the sheet: data[7:0] = d

  // Notes on the sheet:
  //   Escrita
  //   Leitura A
  //   Leitura B
endmodule

module extSinal8bits (
  input  [3:0] imm4,
  output [7:0] imm8
);


  assign imm8 = {{5{imm4[3]}}, imm4[2:0]};
endmodule

module ULA (
  input  [7:0] A,
  input  [7:0] B,
  input  [2:0] Seletor,
  output brzr,
  output [7:0] R
);

  wire [0:0] R3;
  wire [7:0] R0, R1, R2, R4, R5, R6, R7;

  Multiplexer #(.select(3), .width(8)) multiplexer_1 (
    .in0(R0), .in1(R1), .in2(R2), .in3({{7{1'b0}}, R3[0]}), .in4(R4), .in5(R5), .in6(R6), .in7(R7), .out(R),
    .sel(Seletor));
  Adder adder_1 (.a(A), .b(B), .out(R0));  // open: cin, cout
  Subtractor subtractor_1 (.a(A), .b(B), .out(R1));  // open: bin, bout
  assign R2 = A | B;  // OR_Gate or_1, 8 bits wide
  nor nor_1 (R3[0], B[0], B[1], B[2], B[3], B[4], B[5], B[6], B[7]);
  assign R6 = A ^ B;  // XOR_Gate xor_1, 8 bits wide
  slr slr_1 (.A(A), .B(B), .R(R4));
  srr srr_1 (.A(A), .B(B), .R(R5));
  Comparator comparator_1 (.a(A), .b({8{1'b0}}), .eq(brzr));  // open: gt, lt

  // Notes on the sheet:
  //   Add
  //   Sub
endmodule

module slr (
  input  [7:0] A,
  input  [7:0] B,
  output [7:0] R
);

  wire multiplexer_1_out, multiplexer_2_out, multiplexer_3_out, multiplexer_4_out, multiplexer_5_out,
       multiplexer_6_out, multiplexer_7_out, multiplexer_8_out, multiplexer_9_out, multiplexer_10_out,
       multiplexer_11_out, multiplexer_12_out, multiplexer_13_out, multiplexer_14_out, multiplexer_15_out,
       multiplexer_16_out, multiplexer_17_out, multiplexer_18_out, multiplexer_19_out, multiplexer_20_out,
       multiplexer_21_out, multiplexer_22_out, multiplexer_23_out, multiplexer_24_out, or_1_out;

  Multiplexer multiplexer_1 (.in0(A[0]), .in1(1'b0), .out(multiplexer_1_out), .sel(B[0]));
  Multiplexer multiplexer_2 (.in0(A[1]), .in1(A[0]), .out(multiplexer_2_out), .sel(B[0]));
  Multiplexer multiplexer_3 (.in0(A[2]), .in1(A[1]), .out(multiplexer_3_out), .sel(B[0]));
  Multiplexer multiplexer_4 (.in0(A[3]), .in1(A[2]), .out(multiplexer_4_out), .sel(B[0]));
  Multiplexer multiplexer_5 (.in0(A[4]), .in1(A[3]), .out(multiplexer_5_out), .sel(B[0]));
  Multiplexer multiplexer_6 (.in0(A[5]), .in1(A[4]), .out(multiplexer_6_out), .sel(B[0]));
  Multiplexer multiplexer_7 (.in0(A[6]), .in1(A[5]), .out(multiplexer_7_out), .sel(B[0]));
  Multiplexer multiplexer_8 (.in0(A[7]), .in1(A[6]), .out(multiplexer_8_out), .sel(B[0]));
  Multiplexer multiplexer_9 (.in0(multiplexer_1_out), .in1(1'b0), .out(multiplexer_9_out), .sel(B[1]));
  Multiplexer multiplexer_10 (.in0(multiplexer_2_out), .in1(1'b0), .out(multiplexer_10_out), .sel(B[1]));
  Multiplexer multiplexer_11 (.in0(multiplexer_3_out), .in1(multiplexer_1_out), .out(multiplexer_11_out), .sel(B[1]));
  Multiplexer multiplexer_12 (.in0(multiplexer_4_out), .in1(multiplexer_2_out), .out(multiplexer_12_out), .sel(B[1]));
  Multiplexer multiplexer_13 (.in0(multiplexer_5_out), .in1(multiplexer_3_out), .out(multiplexer_13_out), .sel(B[1]));
  Multiplexer multiplexer_14 (.in0(multiplexer_6_out), .in1(multiplexer_4_out), .out(multiplexer_14_out), .sel(B[1]));
  Multiplexer multiplexer_15 (.in0(multiplexer_7_out), .in1(multiplexer_5_out), .out(multiplexer_15_out), .sel(B[1]));
  Multiplexer multiplexer_16 (.in0(multiplexer_8_out), .in1(multiplexer_6_out), .out(multiplexer_16_out), .sel(B[1]));
  Multiplexer multiplexer_17 (.in0(multiplexer_9_out), .in1(1'b0), .out(multiplexer_17_out), .sel(B[2]));
  Multiplexer multiplexer_18 (.in0(multiplexer_10_out), .in1(1'b0), .out(multiplexer_18_out), .sel(B[2]));
  Multiplexer multiplexer_19 (.in0(multiplexer_11_out), .in1(1'b0), .out(multiplexer_19_out), .sel(B[2]));
  Multiplexer multiplexer_20 (.in0(multiplexer_12_out), .in1(1'b0), .out(multiplexer_20_out), .sel(B[2]));
  Multiplexer multiplexer_21 (.in0(multiplexer_13_out), .in1(multiplexer_9_out), .out(multiplexer_21_out), .sel(B[2]));
  Multiplexer multiplexer_22 (.in0(multiplexer_14_out), .in1(multiplexer_10_out), .out(multiplexer_22_out), .sel(B[2]));
  Multiplexer multiplexer_23 (.in0(multiplexer_15_out), .in1(multiplexer_11_out), .out(multiplexer_23_out), .sel(B[2]));
  Multiplexer multiplexer_24 (.in0(multiplexer_16_out), .in1(multiplexer_12_out), .out(multiplexer_24_out), .sel(B[2]));
  Multiplexer multiplexer_25 (.in0(multiplexer_17_out), .in1(1'b0), .out(R[0]), .sel(or_1_out));
  Multiplexer multiplexer_26 (.in0(multiplexer_18_out), .in1(1'b0), .out(R[1]), .sel(or_1_out));
  Multiplexer multiplexer_27 (.in0(multiplexer_19_out), .in1(1'b0), .out(R[2]), .sel(or_1_out));
  Multiplexer multiplexer_28 (.in0(multiplexer_20_out), .in1(1'b0), .out(R[3]), .sel(or_1_out));
  Multiplexer multiplexer_29 (.in0(multiplexer_21_out), .in1(1'b0), .out(R[4]), .sel(or_1_out));
  Multiplexer multiplexer_30 (.in0(multiplexer_22_out), .in1(1'b0), .out(R[5]), .sel(or_1_out));
  Multiplexer multiplexer_31 (.in0(multiplexer_23_out), .in1(1'b0), .out(R[6]), .sel(or_1_out));
  Multiplexer multiplexer_32 (.in0(multiplexer_24_out), .in1(1'b0), .out(R[7]), .sel(or_1_out));
  or or_1 (or_1_out, B[7], B[6], B[5], B[4], B[3]);

  // Other names for the same wires on the sheet: s0 = R[0]; s1 = R[1]; s2 = R[2]; s3 = R[3]; s4 = R[4]; s5 = R[5];
  //   s6 = R[6]; s7 = R[7]
endmodule

module srr (
  input  [7:0] A,
  input  [7:0] B,
  output [7:0] R
);

  wire multiplexer_1_out, multiplexer_2_out, multiplexer_3_out, multiplexer_4_out, multiplexer_5_out,
       multiplexer_6_out, multiplexer_7_out, multiplexer_8_out, multiplexer_9_out, multiplexer_10_out,
       multiplexer_11_out, multiplexer_12_out, multiplexer_13_out, multiplexer_14_out, multiplexer_15_out,
       multiplexer_16_out, multiplexer_17_out, multiplexer_18_out, multiplexer_19_out, multiplexer_20_out,
       multiplexer_21_out, multiplexer_22_out, multiplexer_23_out, multiplexer_24_out, or_1_out;

  Multiplexer multiplexer_1 (.in0(A[0]), .in1(A[1]), .out(multiplexer_1_out), .sel(B[0]));
  Multiplexer multiplexer_2 (.in0(A[1]), .in1(A[2]), .out(multiplexer_2_out), .sel(B[0]));
  Multiplexer multiplexer_3 (.in0(A[2]), .in1(A[3]), .out(multiplexer_3_out), .sel(B[0]));
  Multiplexer multiplexer_4 (.in0(A[3]), .in1(A[4]), .out(multiplexer_4_out), .sel(B[0]));
  Multiplexer multiplexer_5 (.in0(A[4]), .in1(A[5]), .out(multiplexer_5_out), .sel(B[0]));
  Multiplexer multiplexer_6 (.in0(A[5]), .in1(A[6]), .out(multiplexer_6_out), .sel(B[0]));
  Multiplexer multiplexer_7 (.in0(A[6]), .in1(A[7]), .out(multiplexer_7_out), .sel(B[0]));
  Multiplexer multiplexer_8 (.in0(A[7]), .in1(1'b0), .out(multiplexer_8_out), .sel(B[0]));
  Multiplexer multiplexer_9 (.in0(multiplexer_1_out), .in1(multiplexer_3_out), .out(multiplexer_9_out), .sel(B[1]));
  Multiplexer multiplexer_10 (.in0(multiplexer_2_out), .in1(multiplexer_4_out), .out(multiplexer_10_out), .sel(B[1]));
  Multiplexer multiplexer_11 (.in0(multiplexer_3_out), .in1(multiplexer_5_out), .out(multiplexer_11_out), .sel(B[1]));
  Multiplexer multiplexer_12 (.in0(multiplexer_4_out), .in1(multiplexer_6_out), .out(multiplexer_12_out), .sel(B[1]));
  Multiplexer multiplexer_13 (.in0(multiplexer_5_out), .in1(multiplexer_7_out), .out(multiplexer_13_out), .sel(B[1]));
  Multiplexer multiplexer_14 (.in0(multiplexer_6_out), .in1(multiplexer_8_out), .out(multiplexer_14_out), .sel(B[1]));
  Multiplexer multiplexer_15 (.in0(multiplexer_7_out), .in1(1'b0), .out(multiplexer_15_out), .sel(B[1]));
  Multiplexer multiplexer_16 (.in0(multiplexer_8_out), .in1(1'b0), .out(multiplexer_16_out), .sel(B[1]));
  Multiplexer multiplexer_17 (.in0(multiplexer_9_out), .in1(multiplexer_13_out), .out(multiplexer_17_out), .sel(B[2]));
  Multiplexer multiplexer_18 (.in0(multiplexer_10_out), .in1(multiplexer_14_out), .out(multiplexer_18_out), .sel(B[2]));
  Multiplexer multiplexer_19 (.in0(multiplexer_11_out), .in1(multiplexer_15_out), .out(multiplexer_19_out), .sel(B[2]));
  Multiplexer multiplexer_20 (.in0(multiplexer_12_out), .in1(multiplexer_16_out), .out(multiplexer_20_out), .sel(B[2]));
  Multiplexer multiplexer_21 (.in0(multiplexer_13_out), .in1(1'b0), .out(multiplexer_21_out), .sel(B[2]));
  Multiplexer multiplexer_22 (.in0(multiplexer_14_out), .in1(1'b0), .out(multiplexer_22_out), .sel(B[2]));
  Multiplexer multiplexer_23 (.in0(multiplexer_15_out), .in1(1'b0), .out(multiplexer_23_out), .sel(B[2]));
  Multiplexer multiplexer_24 (.in0(multiplexer_16_out), .in1(1'b0), .out(multiplexer_24_out), .sel(B[2]));
  Multiplexer multiplexer_25 (.in0(multiplexer_17_out), .in1(1'b0), .out(R[0]), .sel(or_1_out));
  Multiplexer multiplexer_26 (.in0(multiplexer_18_out), .in1(1'b0), .out(R[1]), .sel(or_1_out));
  Multiplexer multiplexer_27 (.in0(multiplexer_19_out), .in1(1'b0), .out(R[2]), .sel(or_1_out));
  Multiplexer multiplexer_28 (.in0(multiplexer_20_out), .in1(1'b0), .out(R[3]), .sel(or_1_out));
  Multiplexer multiplexer_29 (.in0(multiplexer_21_out), .in1(1'b0), .out(R[4]), .sel(or_1_out));
  Multiplexer multiplexer_30 (.in0(multiplexer_22_out), .in1(1'b0), .out(R[5]), .sel(or_1_out));
  Multiplexer multiplexer_31 (.in0(multiplexer_23_out), .in1(1'b0), .out(R[6]), .sel(or_1_out));
  Multiplexer multiplexer_32 (.in0(multiplexer_24_out), .in1(1'b0), .out(R[7]), .sel(or_1_out));
  or or_1 (or_1_out, B[7], B[6], B[5], B[4], B[3]);

  // Other names for the same wires on the sheet: s0 = R[0]; s1 = R[1]; s2 = R[2]; s3 = R[3]; s4 = R[4]; s5 = R[5];
  //   s6 = R[6]; s7 = R[7]
endmodule

module movhighmovlow (
  input  [7:0] A,
  input  [3:0] imm,
  input  Seletor,
  output [7:0] R
);

  Multiplexer #(.width(8)) multiplexer_1 (.in0({imm, A[3:0]}), .in1({A[7:4], imm}), .out(R), .sel(Seletor));

  // Notes on the sheet:
  //   High
  //   Low
endmodule
